# Fritzing sketch aprilproject (saved by Fritzing 0.9.3b)

parts:
  Part1 = Adafruit Circuit Playground Express [part_number="Adafruit #3333"]
  NEOPIXEL1 = Neopixel Strip -- White (60/m)
  Part2 = DS3231
  JACK1 = 2.1mm Barrel Jack with Terminal Block

nets:
  N1: Part1.D6_A1, NEOPIXEL1.DI
  GND: Part1.GND, NEOPIXEL1.GND#3, Part2.GND
  N2: Part1.D3_A4_SCL, Part2.SCL
  N3: Part1.D2_A5_SDA, Part2.SDA
  N4: Part1.VOUT, Part2.Vin
  N5: NEOPIXEL1.GND#4, JACK1.NEG
  N6: NEOPIXEL1.+5V, JACK1.POS

custom parts:
  Adafruit Circuit Playground Express: Circuit Playground Express is the next step towards a perfect introduction to electronics and programming. We've taken the original Circuit Playground Classic and made it even better! Not only did we pack even more sensors in, we also made it even easier to program. You can now start your journey with Microsoft MakeCode block-based or Javascript programming. Then, you can use the same board to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
  Neopixel Strip -- White (60/m): Neopixel Strip, White, 60 pixels per meter.
  DS3231: The datasheet for the DS3231 explains that this part is an "Extremely Accurate I²C-Integrated RTC/TCXO/Crystal". And, hey, it does exactly what it says on the tin! This Real Time Clock (RTC) is the most precise you can get in a small, low power package. Most RTCs use an external 32kHz timing crystal that is used to keep time with low current draw. And that's all well and good, but those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
