# Fritzing sketch first (saved by Fritzing 0.9.3b)
breadboards: 1

parts:
  LED1 = LED - 5mm [color="Red (633nm)" package="5 mm [THT]"]
  VCC1 = Battery
  R1 = Resistor [tolerance=±5% resistance=220 package=THT]  # not connected

nets:
  N1: LED1.cathode, VCC1.+
  N2: LED1.anode, VCC1.-
